// Logisim project challenge.circ as structural Verilog: 2 circuits, main circuit main
module main (
  input  RST
);

  wire and_1_out, bitselector_1_out, clock_1_out, counter_2_carry, not_1_out;
  wire [2:0] counter_2_q;
  wire [7:0] counter_1_q, decoder_1_out_2, rom_1_data, shift_register_1_q7;

  Clock clock_1 (.out(clock_1_out));
  Counter #(.max('h3f)) counter_1 (.Q(counter_1_q), .clk(counter_2_carry), .clr(RST));  // open: load, D, count, carry
  Counter #(.width(3), .max('h7)) counter_2 (
    .Q(counter_2_q), .carry(counter_2_carry), .clk(clock_1_out), .clr(RST));  // open: load, D, count
  ROM rom_1 (.addr(counter_1_q), .data(rom_1_data));  // open: sel
  not not_1 (not_1_out, clock_1_out);
  BitSelector bitselector_1 (.in(rom_1_data), .out(bitselector_1_out), .sel(counter_2_q));
  and and_1 (and_1_out, not_1_out, counter_2_carry);
  Shift_Register shift_register_1 (
    .in(bitselector_1_out), .clk(not_1_out), .clr(RST), .q0(shift_register_1_q7[7]),
    .q1(shift_register_1_q7[6]), .q2(shift_register_1_q7[5]), .q3(shift_register_1_q7[4]),
    .q4(shift_register_1_q7[3]), .q5(shift_register_1_q7[2]), .q6(shift_register_1_q7[1]),
    .q7(shift_register_1_q7[0]));  // open: shift, out, load, d0, d1, d2, d3, d4, d5, d6, d7
  Hex_Digit_Display hex_digit_display_1 (.value(decoder_1_out_2[7:4]));  // open: dp
  decoder decoder_1 (.in_1(shift_register_1_q7), .out_2(decoder_1_out_2));
  Hex_Digit_Display hex_digit_display_2 (.value(decoder_1_out_2[3:0]), .dp(and_1_out));

  // Notes on the sheet:
  //   contents of rom_1 (hex, n*v repeats v):
  //   50 50 3c 77 32 5a 6 33 73 7d 1a 7 e 2e 36 e 5b f 7d e 36 27 7d 2f 52 27 7d 27 e f 7 27 f 2f 7d 3f e
  //   57 7d 2f 6 7d 1f 7a 1a 27 36 f 2f e 7a 1a 7d 52 e 36 1a 3f e 36 27 27 5f
endmodule

module decoder (
  input  [7:0] in_1,
  output [7:0] out_2
);


  assign out_2 = {in_1[7], in_1[4], in_1[1], in_1[2], in_1[6], in_1[3], in_1[5], in_1[0]};
endmodule
